# Fritzing sketch remoteBME280_SCH (saved by Fritzing 0.9.3b)
circuit board: 7.02655cm x 5.63192cm
breadboards: 1

parts:
  WeMos_D1_Mini1 = WeMos D1 Mini
  LED1 = LED - 5mm [color="Red (633nm)" package="5 mm [THT]"]
  R1 = Resistor [tolerance=±5% resistance=100 package=THT]
  temp1 = Adafruit BME280
  OLED1 = OLED Mono 0.56 inch blue or white

nets:
  3V3: WeMos_D1_Mini1.3V3, temp1.3.3V, OLED1.VCC
  N1: WeMos_D1_Mini1.D1, temp1.SCK/SCL, OLED1.SCL
  N2: WeMos_D1_Mini1.D2, temp1.SDI/SDA, OLED1.SDA
  N3: WeMos_D1_Mini1.D6, R1.Pin_1
  GND: WeMos_D1_Mini1.G, LED1.cathode, temp1.GND, OLED1.GND
  N4: LED1.anode, R1.Pin_0

custom parts:
  Adafruit BME280: Bosch has stepped up their game with their new BME280 sensor, an environmental sensor with temperature, barometric pressure and humidity! This sensor is great for all sorts of weather/environmental sensing and can even be used in both I2C and SPI! This precision sensor from Bosch is the best low-cost sensing solution for measuring humidity with ±3% accuracy, barometric pressure with ±1 hPa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
  OLED Mono 0.56 inch blue or white: OLED, I2C 3.3V - 5V Blue and White text versions

// code stored in the sketch: Untitled2.ino

