# Fritzing sketch remoteDHT11_SCH (saved by Fritzing 0.9.3b)
circuit board: 7.02655cm x 5.63192cm
breadboards: 1

parts:
  WeMos_D1_Mini1 = WeMos D1 Mini
  LED1 = LED - 5mm [color="Red (633nm)" package="5 mm [THT]"]
  dth11 = Humidity and Temperature Sensor RHT03
  R1 = Resistor [tolerance=±5% resistance=100 package=THT]
  R2 = Resistor [tolerance=±5% resistance=4.7 package=THT]
  OLED = OLED Mono 0.56 inch blue or white

nets:
  VCC: WeMos_D1_Mini1.3V3, dth11.Vcc, R2.Pin_0, OLED.VCC
  N1: WeMos_D1_Mini1.D1, OLED.SCL
  N2: WeMos_D1_Mini1.D2, OLED.SDA
  N3: WeMos_D1_Mini1.D5, dth11.Data-signal, R2.Pin_1
  N4: WeMos_D1_Mini1.D6, R1.Pin_1
  N5: WeMos_D1_Mini1.G, LED1.cathode, dth11.GND_1, dth11.GND_2, OLED.GND
  N6: LED1.anode, R1.Pin_0

custom parts:
  OLED Mono 0.56 inch blue or white: OLED, I2C 3.3V - 5V Blue and White text versions

// code stored in the sketch: Untitled2.ino

