# Fritzing sketch remoteSi7021_SCH (saved by Fritzing 0.9.3b)
circuit board: 7.02655cm x 5.63192cm
breadboards: 1

parts:
  WeMos_D1_Mini1 = WeMos D1 Mini
  LED1 = LED - 5mm [color="Red (633nm)" package="5 mm [THT]"]
  R1 = Resistor [tolerance=±5% resistance=100 package=THT]
  Part1 = Adafruit Si7021 Temp Humidity [part_number="Adafruit #3251"]
  Mod1 = OLED Mono 0.56 inch blue or white

nets:
  3V3: WeMos_D1_Mini1.3V3, Part1.+3V3, Mod1.VCC
  N1: WeMos_D1_Mini1.D1, Part1.SCL, Mod1.SCL
  N2: WeMos_D1_Mini1.D2, Part1.SDA, Mod1.SDA
  N3: WeMos_D1_Mini1.D6, R1.Pin_1
  GND: WeMos_D1_Mini1.G, LED1.cathode, Part1.GND, Mod1.GND
  N4: LED1.anode, R1.Pin_0

custom parts:
  Adafruit Si7021 Temp Humidity: It's summer and you're sweating and your hair's all frizzy and all you really want to know is why the weatherman said this morning that today's relative humidity would max out at a perfectly reasonable 42% when it feels more like 77%. Enter the Si7021 Temperature + Humidity Sensor - the best way to prove the weatherman wrong! This lovely sensor for Silicon labs has ± 3% relative humidity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
  OLED Mono 0.56 inch blue or white: OLED, I2C 3.3V - 5V Blue and White text versions

// code stored in the sketch: Untitled2.ino

